# Fritzing sketch Traffic lights with chips_v3 perf board (saved by Fritzing 1.0.6)
breadboards: 3
perfboards: 4

parts:
  A1 = Werner Rothschopf (modified to ESP32-S3-DevKitC dual USB by vanepp Aug 2024)
  Q1 = ULN2803 Darlington Array
  Q2 = ULN2803 Darlington Array
  IC1 = MCP23017 I2C I/O Expander
  R1 = Resistor [tolerance=±5% power=0.25W resistance=4.7k package=THT]
  R2 = Resistor [tolerance=±5% power=0.25W resistance=4.7k package=THT]
  R3 = Resistor [tolerance=±5% power=0.25W resistance=10k package=THT]
  S1 = Pushbutton [package="[THT]"]
  Part1 = Breadboard Power Supply Board SMD
  LED1 = LED - 5mm [color="Red (633nm)" current=0.030A package="5 mm [THT]"]
  LED2 = LED - 5mm [color="Orange (605nm)" current=0.030A package="5 mm [THT]"]
  LED3 = LED - 5mm [color="Green (555nm)" current=0.030A package="5 mm [THT]"]
  LED4 = LED - 5mm [color="Green (555nm)" current=0.030A package="5 mm [THT]"]
  LED5 = LED - 5mm [color="Orange (605nm)" current=0.030A package="5 mm [THT]"]
  LED6 = LED - 5mm [color="Red (633nm)" current=0.030A package="5 mm [THT]"]
  LED7 = LED - 5mm [color="Red (633nm)" current=0.030A package="5 mm [THT]"]
  LED8 = LED - 5mm [color="Orange (605nm)" current=0.030A package="5 mm [THT]"]
  LED9 = LED - 5mm [color="Green (555nm)" current=0.030A package="5 mm [THT]"]
  LED10 = LED - 5mm [color="Red (633nm)" current=0.030A package="5 mm [THT]"]
  LED11 = LED - 5mm [color="Orange (605nm)" current=0.030A package="5 mm [THT]"]
  LED12 = LED - 5mm [color="Green (555nm)" current=0.030A package="5 mm [THT]"]
  R4 = Resistor [tolerance=±5% power=0.25W resistance=220 package=THT]
  R5 = Resistor [tolerance=±5% power=0.25W resistance=220 package=THT]
  R6 = Resistor [tolerance=±5% power=0.25W resistance=220 package=THT]
  R7 = Resistor [tolerance=±5% power=0.25W resistance=220 package=THT]
  R8 = Resistor [tolerance=±5% power=0.25W resistance=220 package=THT]
  R9 = Resistor [tolerance=±5% power=0.25W resistance=220 package=THT]
  R10 = Resistor [tolerance=±5% power=0.25W resistance=220 package=THT]
  R11 = Resistor [tolerance=±5% power=0.25W resistance=220 package=THT]
  R12 = Resistor [tolerance=±5% power=0.25W resistance=220 package=THT]
  R13 = Resistor [tolerance=±5% power=0.25W resistance=220 package=THT]
  R14 = Resistor [tolerance=±5% power=0.25W resistance=220 package=THT]
  R15 = Resistor [tolerance=±5% power=0.25W resistance=220 package=THT]
  Mod1 = KY-021 Mini Magnetic Reed Switch Module [package="Breakout board"]
  A6 = Werner Rothschopf (modified to ESP32-S3-DevKitC dual USB by vanepp Aug 2024)
  Q11 = ULN2803 Darlington Array
  Q12 = ULN2803 Darlington Array
  IC6 = MCP23017 I2C I/O Expander
  R40 = Resistor [tolerance=±5% power=0.25W resistance=4.7k package=THT]
  R41 = Resistor [tolerance=±5% power=0.25W resistance=4.7k package=THT]
  R42 = Resistor [tolerance=±5% power=0.25W resistance=220 package=THT]
  R43 = Resistor [tolerance=±5% power=0.25W resistance=220 package=THT]
  R44 = Resistor [tolerance=±5% power=0.25W resistance=220 package=THT]
  R45 = Resistor [tolerance=±5% power=0.25W resistance=220 package=THT]
  R46 = Resistor [tolerance=±5% power=0.25W resistance=220 package=THT]
  R47 = Resistor [tolerance=±5% power=0.25W resistance=220 package=THT]
  R48 = Resistor [tolerance=±5% power=0.25W resistance=220 package=THT]
  R49 = Resistor [tolerance=±5% power=0.25W resistance=220 package=THT]
  R50 = Resistor [tolerance=±5% power=0.25W resistance=220 package=THT]
  R51 = Resistor [tolerance=±5% power=0.25W resistance=220 package=THT]
  R52 = Resistor [tolerance=±5% power=0.25W resistance=220 package=THT]
  R53 = Resistor [tolerance=±5% power=0.25W resistance=220 package=THT]
  R54 = Resistor [tolerance=±5% power=0.25W resistance=10k package=THT]
  Part4 = Breadboard Power Supply Board SMD
  Mod2 = KY-021 Mini Magnetic Reed Switch Module [package="Breakout board"]
  U2 = Molex Picoblade Series Header [part_number=0533980471 package=Picoblade-53398-0471]
  U3 = Molex Picoblade Series Header [part_number=0533980471 package=Picoblade-53398-0471]
  U4 = Molex Picoblade Series Header [part_number=0533980471 package=Picoblade-53398-0471]
  U5 = Molex Picoblade Series Header [part_number=0533980471 package=Picoblade-53398-0471]
  R27 = Resistor [tolerance=±5% power=0.25W resistance=10k package=THT]
  A5 = Werner Rothschopf (modified to ESP32-S3-DevKitC dual USB by vanepp Aug 2024)
  R36 = Resistor [tolerance=±5% power=0.25W resistance=220 package=THT]
  R28 = Resistor [tolerance=±5% power=0.25W resistance=220 package=THT]
  R39 = Resistor [tolerance=±5% power=0.25W resistance=220 package=THT]
  R25 = Resistor [tolerance=±5% power=0.25W resistance=4.7k package=THT]
  R30 = Resistor [tolerance=±5% power=0.25W resistance=220 package=THT]
  IC5 = MCP23017 I2C I/O Expander
  R35 = Resistor [tolerance=±5% power=0.25W resistance=220 package=THT]
  R34 = Resistor [tolerance=±5% power=0.25W resistance=220 package=THT]
  R37 = Resistor [tolerance=±5% power=0.25W resistance=220 package=THT]
  Q9 = ULN2803 Darlington Array
  Q10 = ULN2803 Darlington Array
  R31 = Resistor [tolerance=±5% power=0.25W resistance=220 package=THT]
  R32 = Resistor [tolerance=±5% power=0.25W resistance=220 package=THT]
  U1 = Molex Picoblade Series Header [part_number=0533980571 package=Picoblade-53398-0571]  # not connected
  R29 = Resistor [tolerance=±5% power=0.25W resistance=220 package=THT]
  R38 = Resistor [tolerance=±5% power=0.25W resistance=220 package=THT]
  R26 = Resistor [tolerance=±5% power=0.25W resistance=4.7k package=THT]  # not connected
  R33 = Resistor [tolerance=±5% power=0.25W resistance=220 package=THT]
  Part3 = Breadboard Power Supply Board SMD  # not connected
  R55 = Resistor [tolerance=±5% power=0.25W resistance=4.7k package=THT]
  R56 = Resistor [tolerance=±5% power=0.25W resistance=4.7k package=THT]
  J4_TL4_+5V_R_Y_G = Molex Picoblade Series Header [part_number=0533980471 package=Picoblade-53398-0471]  # not connected
  J3_TL3_+5V_R_Y_G = Molex Picoblade Series Header [part_number=0533980471 package=Picoblade-53398-0471]  # not connected
  J2_TL2_+5V_R_Y_G = Molex Picoblade Series Header [part_number=0533980471 package=Picoblade-53398-0471]  # not connected
  J1_TL1_+5V_R_Y_G = Molex Picoblade Series Header [part_number=0533980471 package=Picoblade-53398-0471]  # not connected
  S1_KY-021_S_GPIO_sensor_input_+_3V3_-_GND = KY-021 Mini Magnetic Reed Switch Module [package="Breakout board"]  # not connected
  U0_ESP32-S3_GPIO5_SDA_GPIO4_SCL_3V3_logic_GND_shared = Werner Rothschopf (modified to ESP32-S3-DevKitC dual USB by vanepp Aug 2024)
  U3_ULN2803 = ULN2803 Darlington Array  # not connected
  U2_ULN2803 = ULN2803 Darlington Array  # not connected
  U1_MCP23017 = MCP23017 I2C I/O Expander  # not connected
  R14_5_1kΩ_SCL_pull-up_SCL_->_3V3 = Resistor [tolerance=±5% power=0.25W resistance=4.7k package=THT]  # not connected
  R13_5_1kΩ_SDA_pull-up_SDA_->_3V3 = Resistor [tolerance=±5% power=0.25W resistance=4.7k package=THT]  # not connected
  R11_2 = Resistor [tolerance=±5% power=0.25W resistance=220 package=THT]  # not connected
  R3_2 = Resistor [tolerance=±5% power=0.25W resistance=220 package=THT]  # not connected
  R12_2 = Resistor [tolerance=±5% power=0.25W resistance=220 package=THT]  # not connected
  R7_2 = Resistor [tolerance=±5% power=0.25W resistance=220 package=THT]  # not connected
  R4_2 = Resistor [tolerance=±5% power=0.25W resistance=220 package=THT]  # not connected
  R5_2 = Resistor [tolerance=±5% power=0.25W resistance=220 package=THT]  # not connected
  R9_2 = Resistor [tolerance=±5% power=0.25W resistance=220 package=THT]  # not connected
  R10_2 = Resistor [tolerance=±5% power=0.25W resistance=220 package=THT]  # not connected
  R1_2 = Resistor [tolerance=±5% power=0.25W resistance=220 package=THT]  # not connected
  R6_2 = Resistor [tolerance=±5% power=0.25W resistance=220 package=THT]  # not connected
  R2_2 = Resistor [tolerance=±5% power=0.25W resistance=220 package=THT]  # not connected
  R8_2 = Resistor [tolerance=±5% power=0.25W resistance=220 package=THT]  # not connected
  R15_10kΩ_RESET_pull-up_RESET_->_3V3 = Resistor [tolerance=±5% power=0.25W resistance=10k package=THT]  # not connected
  J5_external_LED_power_+5V_LED_GND_shared = Breadboard Power Supply Board SMD  # not connected

nets:
  VDD: A1.Pin_1, A1.Pin_2, IC1.VDD, R1.Pin_0, R2.Pin_0, R3.Pin_0, Mod1.Vin
  N1: A1.Pin_4, IC1.SDA, R2.Pin_1
  N2: A1.Pin_5, IC1.SCL, R1.Pin_1
  N3: A1.Pin_6, Mod1.S
  GND: A1.Pin_22, A1.Pin_23, A1.Pin_44, Q1.GND, Q2.GND, IC1.VSS, IC1.A0, IC1.A1, IC1.A2, S1.Pin_3, S1.Pin_4, Part1.GND, Mod1.-
  N4: Q1.I1, IC1.GPB0
  N5: Q1.I2, IC1.GPB1
  N6: Q1.I3, IC1.GPB2
  N7: Q1.I4, IC1.GPB3
  N8: Q1.I5, IC1.GPB4
  N9: Q1.I6, IC1.GPB5
  N10: Q1.O6, LED4.cathode
  N11: Q1.O5, LED5.cathode
  N12: Q1.O4, LED6.cathode
  N13: Q1.O3, LED3.cathode
  N14: Q1.O2, LED2.cathode
  N15: Q1.O1, LED1.cathode
  N16: Q2.I1, IC1.GPA2
  N17: Q2.I2, IC1.GPA3
  N18: Q2.I3, IC1.GPA4
  N19: Q2.I4, IC1.GPA5
  N20: Q2.I5, IC1.GPA6
  N21: Q2.I6, IC1.GPA7
  N22: Q2.O6, LED12.cathode
  N23: Q2.O5, LED11.cathode
  N24: Q2.O4, LED10.cathode
  N25: Q2.O3, LED9.cathode
  N26: Q2.O2, LED8.cathode
  N27: Q2.O1, LED7.cathode
  N28: IC1.RESET, R3.Pin_1, S1.Pin_1, S1.Pin_2
  N29: Part1.VCC, R4.Pin_0, R5.Pin_0, R6.Pin_0, R7.Pin_0, R8.Pin_0, R9.Pin_0, R10.Pin_0, R11.Pin_0, R12.Pin_0, R13.Pin_0, R14.Pin_0, R15.Pin_0
  N30: LED1.anode, R4.Pin_1
  N31: LED2.anode, R5.Pin_1
  N32: LED3.anode, R6.Pin_1
  N33: LED4.anode, R9.Pin_1
  N34: LED5.anode, R8.Pin_1
  N35: LED6.anode, R7.Pin_1
  N36: LED7.anode, R10.Pin_1
  N37: LED8.anode, R11.Pin_1
  N38: LED9.anode, R12.Pin_1
  N39: LED10.anode, R13.Pin_1
  N40: LED11.anode, R14.Pin_1
  N41: LED12.anode, R15.Pin_1
  N42: A6.Pin_1, A6.Pin_2, R40.Pin_0, R41.Pin_0, R54.Pin_1
  N43: A6.Pin_4, IC6.SDA, R41.Pin_1
  N44: A6.Pin_5, IC6.SCL, R40.Pin_1
  N45: A6.Pin_6, Mod2.S
  N46: A6.Pin_22, A6.Pin_23, A6.Pin_24, A6.Pin_44, IC6.A0, IC6.A1, IC6.A2, Part4.GND, Mod2.-
  N47: Q11.I1, IC6.GPB5
  N48: Q11.I2, IC6.GPB4
  N49: Q11.I3, IC6.GPB3
  N50: Q11.I6, IC6.GPB2
  N51: Q11.I7, IC6.GPB1
  N52: Q11.I8, IC6.GPB0
  GND_2: Q11.GND, Q12.GND
  N53: Q11.O8, R44.Pin_1
  N54: Q11.O7, R48.Pin_1
  N55: Q11.O6, R49.Pin_1
  N56: Q11.O3, R52.Pin_1
  N57: Q11.O2, R43.Pin_1
  N58: Q11.O1, R45.Pin_1
  N59: Q12.I1, IC6.GPA7
  N60: Q12.I2, IC6.GPA6
  N61: Q12.I3, IC6.GPA5
  N62: Q12.I6, IC6.GPA4
  N63: Q12.I7, IC6.GPA3
  N64: Q12.I8, IC6.GPA2
  N65: Q12.O8, R51.Pin_1
  N66: Q12.O7, R53.Pin_1
  N67: Q12.O6, R46.Pin_1
  N68: Q12.O3, R47.Pin_1
  N69: Q12.O2, R42.Pin_1
  N70: Q12.O1, R50.Pin_1
  N71: IC6.RESET, R54.Pin_0
  N72: R42.Pin_0, U4.3
  N73: R43.Pin_0, U2.3
  N74: R44.Pin_0, U3.4
  N75: R45.Pin_0, U2.2
  N76: R46.Pin_0, U5.2
  N77: R47.Pin_0, U4.4
  N78: R48.Pin_0, U3.3
  N79: R49.Pin_0, U3.2
  N80: R50.Pin_0, U4.2
  N81: R51.Pin_0, U5.4
  N82: R52.Pin_0, U2.4
  N83: R53.Pin_0, U5.3
  N84: Part4.VCC, U2.1, U3.1, U4.1, U5.1
  N85: R27.Pin_0, IC5.RESET
  N86: R27.Pin_1, A5.Pin_1, A5.Pin_2, R25.Pin_0, IC5.VDD
  N87: A5.Pin_4, IC5.SDA
  N88: A5.Pin_5, IC5.SCL
  N89: A5.Pin_22, A5.Pin_23, A5.Pin_24, A5.Pin_44, IC5.VSS
  N90: R36.Pin_1, Q9.O4
  N91: R28.Pin_1, Q10.O1
  N92: R39.Pin_1, Q9.O2
  N93: R30.Pin_1, Q10.O3
  N94: IC5.GPB0, Q9.I1
  N95: IC5.GPB1, Q9.I2
  N96: IC5.GPB2, Q9.I3
  N97: IC5.GPB3, Q9.I4
  N98: IC5.GPB4, Q9.I5
  N99: IC5.GPB5, Q9.I6
  N100: IC5.A0, IC5.A1, IC5.A2
  N101: IC5.GPA2, Q10.I1
  N102: IC5.GPA3, Q10.I2
  N103: IC5.GPA4, Q10.I3
  N104: IC5.GPA5, Q10.I4
  N105: IC5.GPA6, Q10.I5
  N106: IC5.GPA7, Q10.I6
  N107: R35.Pin_1, Q9.O1
  N108: R34.Pin_1, Q9.O6
  N109: R37.Pin_1, Q9.O3
  GND_3: Q9.GND, Q10.GND
  N110: Q9.O5, R38.Pin_1
  N111: Q10.O6, R33.Pin_1
  N112: Q10.O5, R32.Pin_1
  N113: Q10.O4, R31.Pin_1
  N114: Q10.O2, R29.Pin_1
  N115: R55.Pin_0, R56.Pin_0
  N116: U0_ESP32-S3_GPIO5_SDA_GPIO4_SCL_3V3_logic_GND_shared.Pin_1, U0_ESP32-S3_GPIO5_SDA_GPIO4_SCL_3V3_logic_GND_shared.Pin_2
  N117: U0_ESP32-S3_GPIO5_SDA_GPIO4_SCL_3V3_logic_GND_shared.Pin_22, U0_ESP32-S3_GPIO5_SDA_GPIO4_SCL_3V3_logic_GND_shared.Pin_23, U0_ESP32-S3_GPIO5_SDA_GPIO4_SCL_3V3_logic_GND_shared.Pin_24, U0_ESP32-S3_GPIO5_SDA_GPIO4_SCL_3V3_logic_GND_shared.Pin_44

custom parts:
  Werner Rothschopf (modified to ESP32-S3-DevKitC dual USB by vanepp Aug 2024): ESP32-S3 ESP32-S3-DevKitC-1 Dual USB development board Pyboard CircuitPython Micropython wifi BLE5.0 ESP32-S3.
  ULN2803 Darlington Array: ULN2803 Darlington Transistor Array with Flyback Protection
  MCP23017 I2C I/O Expander: MCP23017 I2C 16-Channel I/O Expander
  KY-021 Mini Magnetic Reed Switch Module: KY-021 magnetic reed switch module. A reed switch is a magnetic sensor that is normally open and gets closed when exposed to a magnetic field.
